# Fritzing sketch human-trailing (saved by Fritzing 0.9.3b)
breadboards: 1

parts:
  Part1 = Arduino Uno (Rev3) - ICSP
  M1 = DC Motor
  M2 = DC Motor
  R1 = Resistor [tolerance=±5% resistance=220 package="1206 [SMD]"]
  R2 = Resistor [tolerance=±5% resistance=220 package="1206 [SMD]"]
  J1 = Infrared Proximity Sensor
  J2 = Infrared Proximity Sensor
  Part2 = HC-SR04 Ultrasonic Rangemeter
  VCC1 = Battery block 9V

nets:
  N1: Part1.D11_PWM/MOSI, J1.Vout
  N2: Part1.D12/MISO, J2.Vout
  N3: Part1.D2, Part2.Echo
  N4: Part1.D3_PWM, Part2.Trig
  N5: Part1.D4, R1.Pin_0
  N6: Part1.D5_PWM, M1.pin_1
  N7: Part1.D6_PWM, M2.pin_1
  N8: Part1.D7, R2.Pin_0
  VCC: Part1.5V, J1.Vcc, J2.Vcc, Part2.VCC
  GND: Part1.GND, J1.GND, J2.GND, Part2.GND, VCC1.-
  N9: Part1.VIN, VCC1.+
